// Digital circuit Template.dig as structural Verilog
module Template (
  input  P,
  input  Clr,
  input  clock,
  output Z
);

  wire and_1_out, not_1_out, t_ff_1_nq;

  not not_1 (not_1_out, Clr);
  and and_1 (and_1_out, P, not_1_out);
  T_FF t_ff_1 (.T(and_1_out), .C(clock), .nQ(t_ff_1_nq));  // open: Q
  and and_2 (Z, and_1_out, t_ff_1_nq);
endmodule
